# Fritzing sketch circuit 2 (saved by Fritzing 0.9.3b)
breadboards: 1

parts:
  A1 = ESP32 DevKitc V4
  DC_Mot_Enc1 = DC Motor with two-phase hall-encoder [part_number=VT-E-G25A-06-177E]
  U1 = A3144 Hall Effect Sensor. [package="UA [THT]"]
  DC_Mot_Enc2 = DC Motor with two-phase hall-encoder [part_number=VT-E-G25A-06-177E]
  DC_Mot_Enc3 = DC Motor with two-phase hall-encoder [part_number=VT-E-G25A-06-177E]

nets:
  N1: A1.Pin_1, U1.+Vsupply
  N2: A1.Pin_7, U1.Out
  N3: A1.Pin_19, DC_Mot_Enc1.pin1, DC_Mot_Enc1.pin6, DC_Mot_Enc2.pin1, DC_Mot_Enc2.pin6, DC_Mot_Enc3.pin1, DC_Mot_Enc3.pin6
  N4: A1.Pin_26, DC_Mot_Enc3.pin4
  N5: A1.Pin_27, DC_Mot_Enc3.pin3
  N6: A1.Pin_28, DC_Mot_Enc2.pin4
  N7: A1.Pin_29, DC_Mot_Enc2.pin3
  N8: A1.Pin_30, DC_Mot_Enc1.pin4
  N9: A1.Pin_31, DC_Mot_Enc1.pin3
  N10: A1.Pin_32, A1.Pin_38, DC_Mot_Enc1.pin2, DC_Mot_Enc1.pin5, U1.GND, DC_Mot_Enc2.pin2, DC_Mot_Enc2.pin5, DC_Mot_Enc3.pin2, DC_Mot_Enc3.pin5

custom parts:
  ESP32 DevKitc V4: ESP32-DevKitC board with ESP32-WROOM-32 module. ESP32-DevKitC V4 is a small-sized ESP32-based development board produced by Espressif. Most of the pins on the ESP module are broken out to the pin headers on the board. The pins D0, D1, D2, D3, CMD and CLK are used internally for communication between ESP32 and SPI flash memory. They are grouped on both sides near the USB connector. Avoid using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
  A3144 Hall Effect Sensor.: Allegro A3144 hall effect switch for high temperature operation.
