# Fritzing sketch circuit 3 (saved by Fritzing 0.9.3b)
breadboards: 1

parts:
  A1 = ESP32 DevKitc V4
  U1 = A3144 Hall Effect Sensor. [package="UA [THT]"]
  J1 = Basic Servo
  J2 = Basic Servo
  J3 = Basic Servo
  R1 = Trimmer Potentiometer [maximum_resistance=10kΩ package=THT]
  R2 = Trimmer Potentiometer [maximum_resistance=10kΩ package=THT]
  R3 = Trimmer Potentiometer [maximum_resistance=10kΩ package=THT]
  U2 = A3144 Hall Effect Sensor. [package="UA [THT]"]
  U3 = A3144 Hall Effect Sensor. [package="UA [THT]"]
  J4 = Basic Servo
  R4 = Trimmer Potentiometer [maximum_resistance=10kΩ package=THT]
  U4 = A3144 Hall Effect Sensor. [package="UA [THT]"]

nets:
  N1: A1.Pin_1, U1.+Vsupply, U2.+Vsupply, U3.+Vsupply, U4.+Vsupply
  N2: A1.Pin_5, U1.Out
  N3: A1.Pin_7, R1.wiper
  N4: A1.Pin_8, R2.wiper
  N5: A1.Pin_9, R3.wiper
  N6: A1.Pin_10, U2.Out
  N7: A1.Pin_11, U3.Out
  N8: A1.Pin_12, R4.wiper
  N9: A1.Pin_13, U4.Out
  GND: A1.Pin_14, A1.Pin_32, A1.Pin_38, U1.GND, J1.gnd, J2.gnd, J3.gnd, R1.leg1, R2.leg1, R3.leg1, U2.GND, U3.GND, J4.gnd, R4.leg1, U4.GND
  VCC: A1.Pin_18, A1.Pin_19, J1.vcc, J2.vcc, J3.vcc, R1.leg2, R2.leg2, R3.leg2, J4.vcc, R4.leg2

custom parts:
  ESP32 DevKitc V4: ESP32-DevKitC board with ESP32-WROOM-32 module. ESP32-DevKitC V4 is a small-sized ESP32-based development board produced by Espressif. Most of the pins on the ESP module are broken out to the pin headers on the board. The pins D0, D1, D2, D3, CMD and CLK are used internally for communication between ESP32 and SPI flash memory. They are grouped on both sides near the USB connector. Avoid using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
  A3144 Hall Effect Sensor.: Allegro A3144 hall effect switch for high temperature operation.
