# Fritzing sketch circuit (saved by Fritzing 0.9.3b)
breadboards: 1

parts:
  A1 = ESP32 DevKitc V4
  U1 = A3144 Hall Effect Sensor. [package="UA [THT]"]
  DC_Mot_Enc3 = DC Motor with two-phase hall-encoder [part_number=VT-E-G25A-06-177E]
  DC_Mot_Enc1 = DC Motor with two-phase hall-encoder [part_number=VT-E-G25A-06-177E]
  DC_Mot_Enc2 = DC Motor with two-phase hall-encoder [part_number=VT-E-G25A-06-177E]
  L298N1 = L298N DC motor driver
  L298N2 = L298N DC motor driver

nets:
  N1: A1.Pin_1, U1.+Vsupply
  N2: A1.Pin_6, DC_Mot_Enc1.pin3
  N3: A1.Pin_7, DC_Mot_Enc1.pin4
  N4: A1.Pin_8, DC_Mot_Enc2.pin3
  N5: A1.Pin_9, DC_Mot_Enc2.pin4
  N6: A1.Pin_11, DC_Mot_Enc3.pin3
  N7: A1.Pin_12, DC_Mot_Enc3.pin4
  GND: A1.Pin_14, A1.Pin_38, U1.GND, DC_Mot_Enc3.pin2, DC_Mot_Enc3.pin5, DC_Mot_Enc1.pin2, DC_Mot_Enc1.pin5, DC_Mot_Enc2.pin2, DC_Mot_Enc2.pin5, L298N1.GND
  12V: A1.Pin_19, L298N1.12V, L298N2.12V
  N8: A1.Pin_23, L298N1.ENB
  N9: A1.Pin_24, L298N1.IN4
  N10: A1.Pin_25, L298N1.IN3
  N11: A1.Pin_26, L298N1.IN2
  N12: A1.Pin_27, L298N1.IN1
  N13: A1.Pin_28, L298N1.ENA
  N14: A1.Pin_29, L298N2.IN2
  N15: A1.Pin_30, L298N2.IN1
  N16: A1.Pin_33, L298N2.ENA
  N17: DC_Mot_Enc3.pin1, L298N1.OUT1
  N18: DC_Mot_Enc3.pin6, L298N1.OUT2
  N19: DC_Mot_Enc1.pin1, L298N2.OUT1
  N20: DC_Mot_Enc1.pin6, L298N2.OUT2
  N21: DC_Mot_Enc2.pin1, L298N1.OUT4
  N22: DC_Mot_Enc2.pin6, L298N1.OUT3

custom parts:
  ESP32 DevKitc V4: ESP32-DevKitC board with ESP32-WROOM-32 module. ESP32-DevKitC V4 is a small-sized ESP32-based development board produced by Espressif. Most of the pins on the ESP module are broken out to the pin headers on the board. The pins D0, D1, D2, D3, CMD and CLK are used internally for communication between ESP32 and SPI flash memory. They are grouped on both sides near the USB connector. Avoid using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
  A3144 Hall Effect Sensor.: Allegro A3144 hall effect switch for high temperature operation.
  L298N DC motor driver: 2x DC motor driver with 78M05 positive voltage regulator (7..35 V) L298N: max 46 V, 2 A Set 5 V Enable jumper to enable 5 V regultor (needed for the L298N) and +5 V output at screw terminal or supply external +5 V at screw terminal Set ENA and/or ENB to +5 V to enable motor permanently or supply ENA and/or ENB with PWM signal IN1 and IN2 set rotation directory for motor A (OUT1/OUT2) IN2 and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
